# Fritzing sketch ctfalarm_esp32_sketch (saved by Fritzing 0.9.9b)
breadboards: 1

parts:
  S1 = Pushbutton [package="[THT]"]
  S2 = Pushbutton [package="[THT]"]
  S3 = Pushbutton [package="[THT]"]
  S4 = Pushbutton [package="[THT]"]
  S5 = Pushbutton [package="[THT]"]
  Grove2 = Grove 4 Digit Display
  J1 = Piezo Speaker
  WeMos_D1_Mini1 = WeMos D1 Mini  # not connected

nets (from the breadboard view):
  N1: S1.Pin_1, S1.Pin_2, S2.Pin_1, S2.Pin_2, S3.Pin_1, S3.Pin_2, S4.Pin_1, S4.Pin_2, S5.Pin_3, S5.Pin_4, Grove2.GND, J1.pin1
  N2: S1.Pin_3, S1.Pin_4
  N3: S2.Pin_3, S2.Pin_4
  N4: S3.Pin_3, S3.Pin_4
  N5: S4.Pin_3, S4.Pin_4
  N6: S5.Pin_1, S5.Pin_2
