# Fritzing sketch ctfalarm_sketch (saved by Fritzing 0.9.9b)
breadboards: 1

parts:
  Arduino = Arduino Nano (Rev3.0) (ICSP)
  S1 = Pushbutton [package="[THT]"]
  S2 = Pushbutton [package="[THT]"]
  S3 = Pushbutton [package="[THT]"]
  S4 = Pushbutton [package="[THT]"]
  S5 = Pushbutton [package="[THT]"]
  Grove2 = Grove 4 Digit Display
  J1 = Piezo Speaker

nets:
  GND: Arduino.GND, S1.Pin_1, S1.Pin_2, S2.Pin_1, S2.Pin_2, S3.Pin_1, S3.Pin_2, S4.Pin_1, S4.Pin_2, S5.Pin_1, S5.Pin_2, Grove2.GND, J1.pin1
  N1: Arduino.D3, Grove2.CLK
  N2: Arduino.D4, Grove2.DIO
  N3: Arduino.D7, S4.Pin_3, S4.Pin_4
  N4: Arduino.D8, S3.Pin_3, S3.Pin_4
  N5: Arduino.D9, S2.Pin_3, S2.Pin_4
  N6: Arduino.D10, S1.Pin_3, S1.Pin_4
  N7: Arduino.D11/MOSI, J1.pin2
  N8: Arduino.D12/MISO, S5.Pin_3, S5.Pin_4
  3V3: Arduino.3V3, Grove2.VCC
